// Logisim project project_ver_2.circ as structural Verilog: 8 circuits, main circuit Complementor to signed magnitude
module main (
  input  control_2,
  input  control_1,
  input  sign_a,
  input  a1,
  input  a0,
  input  sign_b,
  input  b1,
  input  b0
);

  wire alu_1_add, alu_1_division_by_zero, alu_1_multiply, alu_1_r0, alu_1_r1, alu_1_r2, alu_1_r3,
       alu_1_reamainer, alu_1_sign, alu_1_subtract, alu_1_zero_output, and_1_out, and_2_out, and_3_out,
       and_4_out, and_5_out, and_6_out, n7448_1_p10, n7448_1_p11, n7448_1_p12, n7448_1_p13, n7448_1_p14,
       n7448_1_p15, n7448_1_p16, not_1_out;

  LED zero_output (.in(alu_1_zero_output));
  LED MULTIPLY (.in(alu_1_multiply));
  LED SUBTRACT (.in(alu_1_subtract));
  LED REMAINDER (.in(alu_1_reamainer));
  LED Division_by_zero (.in(alu_1_division_by_zero));
  LED ADD (.in(alu_1_add));
  ALU alu_1 (
    .control_1(control_1), .control_2(control_2), .sign_a(sign_a), .a1(a1), .a0(a0), .sign_b(sign_b),
    .b1(b1), .b0(b0), .Sign(alu_1_sign), .r1(alu_1_r1), .r2(alu_1_r2), .r3(alu_1_r3), .r0(alu_1_r0),
    .Zero_Output(alu_1_zero_output), .Division_By_Zero(alu_1_division_by_zero), .ADD(alu_1_add),
    .SUBTRACT(alu_1_subtract), .MULTIPLY(alu_1_multiply), .REAMAINER(alu_1_reamainer));
  not not_1 (not_1_out, alu_1_division_by_zero);
  LED sign (.in(alu_1_sign));
  _7_Segment_Display u_7_segment_display_1 (
    .g(alu_1_sign), .f(1'b0), .a(1'b0), .b(1'b0), .e(1'b0), .d(1'b0), .c(1'b0), .dp(1'b0));
  // _7448 7448_1: pin names not known; wires that end beside it: alu_1_r1, alu_1_r2, 1'b1, 1'b1, 1'b1, alu_1_r3, alu_1_r0, 1'b0, 1'b1, n7448_1_p10, n7448_1_p11, n7448_1_p12, n7448_1_p13, n7448_1_p14, n7448_1_p15, n7448_1_p16
  and and_1 (and_1_out, n7448_1_p10, not_1_out);
  _7_Segment_Display u_7_segment_display_2 (
    .g(n7448_1_p11), .f(and_1_out), .a(and_4_out), .b(and_3_out), .e(and_2_out), .d(and_6_out),
    .c(and_5_out), .dp(1'b0));
  and and_2 (and_2_out, n7448_1_p16, not_1_out);
  and and_3 (and_3_out, n7448_1_p13, not_1_out);
  and and_4 (and_4_out, n7448_1_p12, not_1_out);
  and and_5 (and_5_out, n7448_1_p14, not_1_out);
  and and_6 (and_6_out, n7448_1_p15, not_1_out);
endmodule

module Complementor_to_signed_magnitude (
  input  s1,
  input  x2,
  input  x1,
  output s1_2,
  output r2,
  output r1
);

  wire xor_1_out, xor_2_out;

  xor xor_1 (xor_1_out, x1, s1);
  xor xor_2 (xor_2_out, x2, s1);
  compementor_addar compementor_addar_1 (.c1(s1), .x1(xor_1_out), .y1(xor_2_out), .output_2(r2), .output_1(r1));

  assign s1_2 = s1;
endmodule

module compementor_addar (
  input  c1,
  input  x1,
  input  y1,
  output output_2,
  output output_1
);

  wire and_1_out;

  xor xor_1 (output_1, c1, x1);
  and and_1 (and_1_out, c1, x1);
  xor xor_2 (output_2, y1, and_1_out);
endmodule

module FUll_ADDAR (
  input  c,
  input  x,
  input  y,
  output carry,
  output s1
);

  wire and_1_out, and_2_out, xor_1_out;

  and and_1 (and_1_out, x, y);
  xor xor_1 (xor_1_out, x, y);
  xor xor_2 (s1, c, xor_1_out);
  and and_2 (and_2_out, c, xor_1_out);
  or or_1 (carry, and_2_out, and_1_out);
endmodule

// remind
module Remainder (
  input  sign_1,
  input  a2,
  input  a1,
  input  sign_2,
  input  b2,
  input  b1,
  input  control,
  output sign,
  output s4,
  output s3,
  output s2,
  output s0,
  output Divison_By_Zero
);

  wire and_2_out, and_3_out, and_4_out, and_5_out, and_6_out, and_7_out, and_8_out, and_9_out, and_10_out,
       and_12_out, and_13_out, not_1_out, not_2_out, not_3_out, not_4_out, not_5_out;

  and and_1 (sign, sign_1, control);
  and and_2 (and_2_out, a2, control);
  and and_3 (and_3_out, a1, control);
  and and_4 (and_4_out, b2, control);
  and and_5 (and_5_out, b1, control);
  not not_1 (not_1_out, and_3_out);
  not not_2 (not_2_out, and_2_out);
  not not_3 (not_3_out, and_4_out);
  not not_4 (not_4_out, and_5_out);
  and and_6 (and_6_out, and_2_out, not_1_out);
  and and_7 (and_7_out, and_4_out, and_5_out);
  and and_8 (and_8_out, not_2_out, and_3_out);
  and and_9 (and_9_out, and_3_out, and_4_out);
  not not_5 (not_5_out, and_5_out);
  and and_10 (and_10_out, not_3_out, not_4_out);
  and and_11 (s2, and_6_out, and_7_out);
  and and_12 (and_12_out, and_8_out, and_4_out);
  or or_1 (s0, and_12_out, and_13_out);
  and and_13 (and_13_out, and_9_out, not_5_out);
  and and_14 (Divison_By_Zero, and_10_out, control);

  assign s3 = 1'b0;
  assign s4 = 1'b0;
endmodule

// Multiply
module Multiplayer (
  input  sign_1,
  input  a2,
  input  a1,
  input  sing_2,
  input  b2,
  input  b1,
  input  control,
  output c4_sign,
  output c3,
  output c2,
  output c1,
  output c0
);

  wire and_1_out, and_2_out, and_3_out, and_4_out, b1_a1_out, b1_a2_out, b2_a1_out, b2_a2_out,
       full_addar_1_carry, full_addar_2_carry;

  and and_1 (and_1_out, a2, control);
  and and_2 (and_2_out, a1, control);
  and and_3 (and_3_out, b2, control);
  and and_4 (and_4_out, b1, control);
  and b1_a1 (b1_a1_out, and_2_out, and_4_out);
  and b1_a2 (b1_a2_out, and_1_out, and_4_out);
  and b2_a1 (b2_a1_out, and_2_out, and_3_out);
  and b2_a2 (b2_a2_out, and_1_out, and_3_out);
  xor sign (c4_sign, sign_1, sing_2);
  FUll_ADDAR full_addar_1 (.c(b1_a1_out), .x(1'b0), .y(1'b0), .carry(full_addar_1_carry), .s1(c0));
  FUll_ADDAR full_addar_2 (.c(full_addar_1_carry), .x(b1_a2_out), .y(b2_a1_out), .carry(full_addar_2_carry), .s1(c1));
  FUll_ADDAR full_addar_3 (.c(full_addar_2_carry), .x(b2_a2_out), .y(1'b0), .carry(c3), .s1(c2));
endmodule

// Add-sub
module Addar_sub (
  input  a1,
  input  b1,
  input  carry1,
  input  carry2,
  input  a2,
  input  b2,
  output sign,
  output s4,
  output s3,
  output s2,
  output s1
);

  wire and_1_out, and_2_out, and_3_out, and_4_out, complementor_to_signed_magnitude_1_s1_2,
       full_addar_1_carry, full_addar_1_s1, full_addar_2_carry, full_addar_2_s1, not_1_out, not_2_out,
       not_3_out, or_1_out, or_2_out, or_3_out, xor_1_out, xor_2_out, xor_3_out, xor_4_out, xor_5_out,
       xor_6_out;

  and and_1 (and_1_out, carry2, carry1);
  not not_1 (not_1_out, carry2);
  not not_2 (not_2_out, carry1);
  xor xor_1 (xor_1_out, a1, and_2_out);
  xor xor_2 (xor_2_out, b1, and_3_out);
  and and_2 (and_2_out, carry1, not_1_out);
  and and_3 (and_3_out, carry2, not_2_out);
  xor xor_3 (xor_3_out, a2, and_2_out);
  xor xor_4 (xor_4_out, b2, and_3_out);
  or or_1 (or_1_out, xor_5_out, 1'b0);
  xor xor_5 (xor_5_out, carry1, carry2);
  FUll_ADDAR full_addar_1 (
    .c(or_1_out), .x(xor_1_out), .y(xor_2_out), .carry(full_addar_1_carry), .s1(full_addar_1_s1));
  FUll_ADDAR full_addar_2 (
    .c(full_addar_1_carry), .x(xor_3_out), .y(xor_4_out), .carry(full_addar_2_carry), .s1(full_addar_2_s1));
  and and_4 (and_4_out, full_addar_2_carry, xor_5_out);
  xor xor_6 (xor_6_out, or_1_out, and_4_out);
  Complementor_to_signed_magnitude complementor_to_signed_magnitude_1 (
    .s1(xor_6_out), .x2(full_addar_2_s1), .x1(full_addar_1_s1),
    .s1_2(complementor_to_signed_magnitude_1_s1_2), .r2(s2), .r1(s1));
  not not_3 (not_3_out, xor_5_out);
  and and_5 (s3, full_addar_2_carry, not_3_out);
  or or_2 (or_2_out, and_1_out, complementor_to_signed_magnitude_1_s1_2);
  or or_3 (or_3_out, s3, s2, s1);
  and and_6 (sign, or_2_out, or_3_out);

  assign s4 = 1'b0;
endmodule

module ALU (
  input  control_2,
  input  control_1,
  input  sign_a,
  input  a1,
  input  a0,
  input  sign_b,
  input  b1,
  input  b0,
  output ADD,
  output SUBTRACT,
  output MULTIPLY,
  output REAMAINER,
  output Sign,
  output r1,
  output r2,
  output r3,
  output r0,
  output Zero_Output,
  output Division_By_Zero
);

  wire add_2_out, add_3_out, add_4_out, add_5_out, add_6_out, add_out, addar_sub_1_s1, addar_sub_1_s2,
       addar_sub_1_s3, addar_sub_1_s4, addar_sub_1_sign, and_1_out, multiplayer_1_c0, multiplayer_1_c1,
       multiplayer_1_c2, multiplayer_1_c3, multiplayer_1_c4_sign, not_1_out, not_2_out, not_3_out, not_4_out,
       not_5_out, not_6_out, not_7_out, or_1_out, or_2_out, or_3_out, or_4_out, or_5_out, remainder_1_s0,
       remainder_1_s2, remainder_1_s3, remainder_1_s4, remainder_1_sign, xor_1_out;

  Remainder remainder_1 (
    .sign_1(sign_a), .a2(a1), .a1(a0), .sign_2(sign_b), .b2(b1), .b1(b0), .control(REAMAINER),
    .sign(remainder_1_sign), .s4(remainder_1_s4), .s3(remainder_1_s3), .s2(remainder_1_s2),
    .s0(remainder_1_s0), .Divison_By_Zero(Division_By_Zero));
  xor xor_1 (xor_1_out, SUBTRACT, sign_b);
  Multiplayer multiplayer_1 (
    .sign_1(sign_a), .a2(a1), .a1(a0), .sing_2(sign_b), .b2(b1), .b1(b0), .control(MULTIPLY),
    .c4_sign(multiplayer_1_c4_sign), .c3(multiplayer_1_c3), .c2(multiplayer_1_c2), .c1(multiplayer_1_c1),
    .c0(multiplayer_1_c0));
  not not_1 (not_1_out, control_2);
  not not_2 (not_2_out, control_1);
  not not_3 (not_3_out, control_2);
  not not_4 (not_4_out, control_1);
  and u_add (add_out, or_1_out, sign_a);
  and add_2 (add_2_out, or_1_out, a1);
  and add_3 (add_3_out, or_1_out, a0);
  and add_4 (add_4_out, or_1_out, xor_1_out);
  and add_5 (add_5_out, or_1_out, b1);
  and add_6 (add_6_out, or_1_out, b0);
  and add_7 (ADD, not_1_out, not_2_out);
  and u_subtract (SUBTRACT, not_3_out, control_1);
  and multply (MULTIPLY, control_2, not_4_out);
  and reminder (REAMAINER, control_2, control_1);
  and and_1 (and_1_out, MULTIPLY, multiplayer_1_c4_sign);
  or or_1 (or_1_out, ADD, SUBTRACT);
  Addar_sub addar_sub_1 (
    .a1(add_3_out), .b1(add_6_out), .carry1(add_out), .carry2(add_4_out), .a2(add_2_out), .b2(add_5_out),
    .sign(addar_sub_1_sign), .s4(addar_sub_1_s4), .s3(addar_sub_1_s3), .s2(addar_sub_1_s2),
    .s1(addar_sub_1_s1));
  or a3 (r3, remainder_1_s4, addar_sub_1_s4, multiplayer_1_c3);
  or a2 (r2, remainder_1_s3, addar_sub_1_s3, multiplayer_1_c2);
  or u_a1 (r1, remainder_1_s2, addar_sub_1_s2, multiplayer_1_c1);
  or u_a0 (r0, remainder_1_s0, addar_sub_1_s1, multiplayer_1_c0);
  or or_2 (or_2_out, and_1_out, addar_sub_1_sign, remainder_1_sign);
  and and_2 (Sign, or_2_out, not_5_out);
  not not_5 (not_5_out, not_6_out);
  or or_3 (or_3_out, r3, r0);
  or or_4 (or_4_out, or_3_out, or_5_out);
  or or_5 (or_5_out, r1, r2);
  not not_6 (not_6_out, or_4_out);
  not not_7 (not_7_out, Division_By_Zero);
  and and_3 (Zero_Output, not_7_out, not_6_out);
endmodule
